# Fritzing sketch Reaction game (saved by Fritzing 0.9.9b)
circuit board: 8.46667cm x 5.64444cm
breadboards: 1

parts:
  Onderdeel1 = Arduino Uno (Rev3)
  S1 = Pushbutton [package="[THT]"]
  R1 = Resistor [tolerance=±5% power=0.25 resistance=220 package=THT]
  U1 = 74HC595 [package="DIP16 [THT]"]
  U2 = 7-SEGMENT-DISPLAY [package=7-segment-display]

nets:
  N1: Onderdeel1.D2, S1.Pin_3, S1.Pin_4
  N2: Onderdeel1.D3_PWM, U1.DS
  N3: Onderdeel1.D4, U1.ST_CP
  N4: Onderdeel1.D5_PWM, U1.SH_CP
  5V: Onderdeel1.5V, U1.VCC
  N5: Onderdeel1.GND, R1.Pin_0, U1.OE
  N6: S1.Pin_1, S1.Pin_2, R1.Pin_1
  N7: U1.Q0, U2.D
